# Fritzing sketch UVtester (saved by Fritzing 1.0.2b)
circuit board: 8.46667cm x 5.64444cm
breadboards: 1

parts:
  WeMos_D1_Mini1 = WeMos D1 Mini
  Part1 = GUVA-S12SD UV Light Sensor

nets:
  3V3: WeMos_D1_Mini1.3V3, Part1.5V
  N1: WeMos_D1_Mini1.A0, Part1.Out
  GND: WeMos_D1_Mini1.G, Part1.GND

custom parts:
  GUVA-S12SD UV Light Sensor: Extend your light-sensing spectrum with this analog UV sensor module. It uses a UV photodiode, which can detect the 240-370nm range of light (which covers UVB and most of UVA spectrum). The signal level from the photodiode is very small, in the nano-ampere level, so we tossed on an opamp to amplify the signal to a more manageable volt-level.
